# Fritzing sketch Dog-box (saved by Fritzing 0.9.3b)
breadboards: 1

parts:
  Part1 = Photon
  hc-sr1 = hc-sr04
  Part2 = Adafruit Mini TFT Display - 0.96in 160x80 [part_number="Adafruit 3533"]
  S1 = Pushbutton [package="[SMD]"]
  J1 = Basic Servo
  R1 = Resistor [tolerance=±5% resistance=10k package=THT]

nets:
  N1: Part1.A0, Part2.DC
  N2: Part1.A1, Part2.TFTRST
  N3: Part1.A2, Part2.TFTCS
  N4: Part1.A3, Part2.SCK
  N5: Part1.A4, Part2.MISO
  N6: Part1.A5, Part2.MOSI
  GND: Part1.GND, hc-sr1.GND, Part2.GND, J1.gnd, R1.Pin_0
  VIN: Part1.VIN, hc-sr1.VCC, Part2.VIN, S1.Pin_1, S1.Pin_2, J1.vcc
  N7: Part1.D0, J1.pulse
  N8: Part1.D2, hc-sr1.Trig
  N9: Part1.D5, S1.Pin_3, S1.Pin_4, R1.Pin_1
  N10: Part1.D6, hc-sr1.Echo

custom parts:
  Adafruit Mini TFT Display - 0.96in 160x80: It's the size of your thumbnail, with glorious 160x80 pixel color... it's the Adafruit Mini TFT Breakout! This very very small display is only 0.96" diagonal, packed with RGB pixels, for making very small high-density displays. The display uses 4-wire SPI to communicate and has its own pixel-addressable frame buffer, it can be used with every kind of microcontroller. Even a very small one with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
